# Fritzing sketch SmartCoffeeMachine (saved by Fritzing 0.9.3b)
breadboards: 1

parts:
  Componente1 = Arduino Uno (Rev3)
  R1 = Resistor [tolerance=±5% resistance=220 package=THT]
  R2 = Resistor [tolerance=±5% resistance=220 package=THT]
  R3 = Resistor [tolerance=±5% resistance=220 package=THT]
  R5 = Resistor [tolerance=±5% resistance=10k package=THT]
  LED1 = LED - 5mm [color="Green (555nm)" package="5 mm [THT]"]
  LED2 = LED - 5mm [color="Green (555nm)" package="5 mm [THT]"]
  LED3 = LED - 5mm [color="Green (555nm)" package="5 mm [THT]"]
  PIR1 = PIR sensor
  U1 = HC-SR04 [chip_label=IC package="SIP (Single Inline) [THT]"]
  S1 = Pushbutton [package="[SMD]"]
  R6 = Rotary Potentiometer (Small) [maximum_resistance=100kΩ package=THT]

nets:
  N1: Componente1.A1, R6.wiper
  N2: Componente1.D8, PIR1.SIG
  N3: Componente1.D9_PWM, U1.Trig
  N4: Componente1.D10_PWM/SS, U1.Echo
  N5: Componente1.D2, LED2.anode
  5V: Componente1.D3_PWM, Componente1.5V, LED1.anode, PIR1.VDD, U1.Vcc, S1.Pin_1, S1.Pin_2, R6.leg2
  N6: Componente1.D4, LED3.anode
  N7: Componente1.D5_PWM, R5.Pin_0, S1.Pin_3, S1.Pin_4
  GND: Componente1.GND, R1.Pin_1, R2.Pin_0, R3.Pin_1, R5.Pin_1, PIR1.GND, U1.GND, R6.leg1
  N8: R1.Pin_0, LED2.cathode
  N9: R2.Pin_1, LED3.cathode
  N10: R3.Pin_0, LED1.cathode

custom parts:
  HC-SR04: HC-SR04 ultrasound distance sensor
